// Logisim project Display numbers 0-9.circ as structural Verilog: 8 circuits, main circuit main
module S1 (
  input  a,
  input  b,
  input  c,
  input  d,
  output x
);

  wire and_1_out, and_2_out, and_3_out, and_4_out, not_1_out, not_2_out, not_3_out, not_4_out, not_5_out,
       not_6_out, not_7_out, not_8_out, not_9_out;

  not not_1 (not_1_out, b);
  not not_2 (not_2_out, c);
  not not_3 (not_3_out, d);
  not not_4 (not_4_out, a);
  not not_5 (not_5_out, c);
  not not_6 (not_6_out, a);
  not not_7 (not_7_out, d);
  not not_8 (not_8_out, b);
  not not_9 (not_9_out, c);
  and and_1 (and_1_out, not_1_out, not_2_out, not_3_out);
  and and_2 (and_2_out, not_4_out, b, not_5_out);
  and and_3 (and_3_out, not_6_out, b, c, not_7_out);
  and and_4 (and_4_out, a, not_8_out, not_9_out, d);
  or or_1 (x, and_1_out, and_2_out, and_3_out, and_4_out);
endmodule

module S2 (
  input  a,
  input  b,
  input  c,
  input  d,
  output x
);

  wire and_1_out, and_2_out, and_3_out, and_4_out, and_5_out, not_1_out, not_2_out, not_3_out, not_4_out,
       not_5_out, not_6_out, not_7_out, not_8_out, not_9_out, not_10_out;

  not not_1 (not_1_out, a);
  not not_2 (not_2_out, b);
  not not_3 (not_3_out, d);
  not not_4 (not_4_out, a);
  not not_5 (not_5_out, a);
  not not_6 (not_6_out, c);
  not not_7 (not_7_out, a);
  not not_8 (not_8_out, d);
  not not_9 (not_9_out, b);
  not not_10 (not_10_out, c);
  and and_1 (and_1_out, not_1_out, not_2_out, not_3_out);
  and and_2 (and_2_out, not_4_out, c, d);
  and and_3 (and_3_out, not_5_out, b, not_6_out, d);
  and and_4 (and_4_out, not_7_out, b, c, not_8_out);
  and and_5 (and_5_out, a, not_9_out, not_10_out);
  or or_1 (x, and_1_out, and_2_out, and_3_out, and_4_out, and_5_out);
endmodule

module S3 (
  input  a,
  input  b,
  input  c,
  input  d,
  output x
);

  wire and_1_out, and_2_out, and_3_out, and_4_out, not_1_out, not_2_out, not_3_out, not_4_out, not_5_out,
       not_6_out, not_7_out, not_8_out, not_9_out;

  not not_1 (not_1_out, b);
  not not_2 (not_2_out, c);
  not not_3 (not_3_out, a);
  not not_4 (not_4_out, b);
  not not_5 (not_5_out, d);
  not not_6 (not_6_out, a);
  not not_7 (not_7_out, a);
  not not_8 (not_8_out, c);
  not not_9 (not_9_out, d);
  and and_1 (and_1_out, not_1_out, not_2_out);
  and and_2 (and_2_out, not_3_out, not_4_out, c, not_5_out);
  and and_3 (and_3_out, not_6_out, c, d);
  and and_4 (and_4_out, not_7_out, b, not_8_out, not_9_out);
  or or_1 (x, and_1_out, and_2_out, and_3_out, and_4_out);
endmodule

module S4 (
  input  a,
  input  b,
  input  c,
  output x
);

  wire and_1_out, and_2_out, and_3_out, not_1_out, not_2_out, not_3_out, not_4_out, not_5_out;

  not not_1 (not_1_out, a);
  and and_1 (and_1_out, not_1_out, c);
  not not_2 (not_2_out, a);
  and and_2 (and_2_out, not_2_out, b, not_3_out);
  not not_3 (not_3_out, c);
  and and_3 (and_3_out, a, not_4_out, not_5_out);
  not not_4 (not_4_out, b);
  not not_5 (not_5_out, c);
  or or_1 (x, and_1_out, and_2_out, and_3_out);
endmodule

module S5 (
  input  a,
  input  b,
  input  c,
  input  d,
  output x
);

  wire and_1_out, and_2_out, and_3_out, not_1_out, not_2_out, not_3_out, not_4_out, not_5_out, not_6_out,
       not_7_out, not_8_out;

  not not_1 (not_1_out, b);
  not not_2 (not_2_out, a);
  not not_3 (not_3_out, d);
  not not_4 (not_4_out, a);
  not not_5 (not_5_out, d);
  not not_6 (not_6_out, b);
  not not_7 (not_7_out, c);
  not not_8 (not_8_out, d);
  and and_1 (and_1_out, not_1_out, not_2_out, not_3_out);
  and and_2 (and_2_out, not_4_out, b, c, not_5_out);
  or or_1 (x, and_1_out, and_2_out, and_3_out);
  and and_3 (and_3_out, a, not_6_out, not_7_out, not_8_out);
endmodule

module S6 (
  input  a,
  input  b,
  input  c,
  input  d,
  output x
);

  wire and_1_out, and_2_out, and_3_out, and_4_out, and_5_out, not_1_out, not_2_out, not_3_out, not_4_out,
       not_5_out, not_6_out, not_7_out, not_8_out, not_9_out, not_10_out, not_11_out;

  not not_1 (not_1_out, a);
  not not_2 (not_2_out, b);
  not not_3 (not_3_out, d);
  not not_4 (not_4_out, a);
  not not_5 (not_5_out, b);
  not not_6 (not_6_out, a);
  not not_7 (not_7_out, c);
  not not_8 (not_8_out, a);
  not not_9 (not_9_out, d);
  not not_10 (not_10_out, b);
  not not_11 (not_11_out, c);
  and and_1 (and_1_out, not_1_out, not_2_out, not_3_out);
  and and_2 (and_2_out, not_4_out, not_5_out, c);
  and and_3 (and_3_out, not_6_out, b, not_7_out, d);
  and and_4 (and_4_out, not_8_out, b, c, not_9_out);
  and and_5 (and_5_out, a, not_10_out, not_11_out);
  or or_1 (x, and_1_out, and_2_out, and_3_out, and_4_out, and_5_out);
endmodule

module S7 (
  input  a,
  input  b,
  input  c,
  input  d,
  output x
);

  wire and_1_out, and_2_out, and_3_out, and_4_out, not_1_out, not_2_out, not_3_out, not_4_out, not_5_out,
       not_6_out, not_7_out, not_8_out;

  not not_1 (not_1_out, a);
  and and_1 (and_1_out, not_1_out, not_2_out, not_3_out);
  not not_2 (not_2_out, b);
  not not_3 (not_3_out, c);
  not not_4 (not_4_out, a);
  and and_2 (and_2_out, not_4_out, not_5_out, d);
  not not_5 (not_5_out, b);
  not not_6 (not_6_out, a);
  and and_3 (and_3_out, not_6_out, b);
  and and_4 (and_4_out, a, not_7_out, not_8_out);
  not not_7 (not_7_out, b);
  not not_8 (not_8_out, c);
  or or_1 (x, and_1_out, and_2_out, and_3_out, and_4_out);
endmodule

module main (
  input  a,
  input  b,
  input  c,
  input  d,
  input  in_5
);

  wire and_1_out, and_2_out, and_3_out, and_4_out, and_5_out, and_6_out, and_7_out, and_8_out, and_9_out,
       and_10_out, and_11_out, and_12_out, and_13_out, and_14_out, and_15_out, and_16_out, and_17_out,
       and_18_out, and_19_out, and_20_out, and_21_out, and_22_out, and_23_out, and_24_out, and_25_out,
       and_26_out, and_27_out, and_28_out, not_1_out, not_2_out, not_3_out, not_4_out, not_5_out, not_6_out,
       not_7_out, not_8_out, not_9_out, not_10_out, not_11_out, not_12_out, not_13_out, not_14_out,
       not_15_out, not_16_out, not_17_out, not_18_out, not_19_out, not_20_out, not_21_out, not_22_out,
       not_23_out, not_24_out, not_25_out, not_26_out, not_27_out, not_28_out, not_29_out, not_30_out,
       not_31_out, not_32_out, not_33_out, not_34_out, not_35_out, not_36_out, not_37_out, not_38_out,
       not_39_out, not_40_out, not_41_out, not_42_out, not_43_out, not_44_out, not_45_out, not_46_out,
       not_47_out, not_48_out, not_49_out, not_50_out, not_51_out, not_52_out, not_53_out, not_54_out,
       not_55_out, not_56_out, not_57_out, not_58_out, not_59_out, not_60_out, or_1_out, or_2_out, or_3_out,
       or_4_out, or_5_out, or_6_out, or_7_out;

  not not_1 (not_1_out, b);
  not not_2 (not_2_out, c);
  not not_3 (not_3_out, d);
  not not_4 (not_4_out, a);
  not not_5 (not_5_out, c);
  not not_6 (not_6_out, a);
  not not_7 (not_7_out, d);
  not not_8 (not_8_out, b);
  not not_9 (not_9_out, c);
  not not_10 (not_10_out, a);
  not not_11 (not_11_out, b);
  not not_12 (not_12_out, d);
  not not_13 (not_13_out, a);
  not not_14 (not_14_out, a);
  not not_15 (not_15_out, c);
  not not_16 (not_16_out, a);
  not not_17 (not_17_out, d);
  not not_18 (not_18_out, b);
  not not_19 (not_19_out, c);
  not not_20 (not_20_out, b);
  not not_21 (not_21_out, c);
  not not_22 (not_22_out, a);
  not not_23 (not_23_out, b);
  not not_24 (not_24_out, d);
  not not_25 (not_25_out, a);
  not not_26 (not_26_out, a);
  not not_27 (not_27_out, c);
  not not_28 (not_28_out, d);
  and and_1 (and_1_out, not_1_out, not_2_out, not_3_out);
  and and_2 (and_2_out, not_4_out, b, not_5_out);
  and and_3 (and_3_out, not_6_out, b, c, not_7_out);
  and and_4 (and_4_out, a, not_8_out, not_9_out, d);
  and and_5 (and_5_out, not_10_out, not_11_out, not_12_out);
  and and_6 (and_6_out, not_13_out, c, d);
  and and_7 (and_7_out, not_14_out, b, not_15_out, d);
  and and_8 (and_8_out, not_16_out, b, c, not_17_out);
  and and_9 (and_9_out, a, not_18_out, not_19_out);
  and and_10 (and_10_out, not_20_out, not_21_out);
  and and_11 (and_11_out, not_22_out, not_23_out, c, not_24_out);
  and and_12 (and_12_out, not_25_out, c, d);
  and and_13 (and_13_out, not_26_out, b, not_27_out, not_28_out);
  not not_29 (not_29_out, a);
  and and_14 (and_14_out, not_29_out, not_30_out, not_31_out);
  not not_30 (not_30_out, b);
  not not_31 (not_31_out, c);
  not not_32 (not_32_out, a);
  and and_15 (and_15_out, not_32_out, not_33_out, d);
  not not_33 (not_33_out, b);
  not not_34 (not_34_out, a);
  and and_16 (and_16_out, not_34_out, b);
  not not_35 (not_35_out, b);
  and and_17 (and_17_out, a, not_35_out, not_36_out);
  not not_36 (not_36_out, c);
  or or_1 (or_1_out, and_1_out, and_2_out, and_3_out, and_4_out);
  or or_2 (or_2_out, and_5_out, and_6_out, and_7_out, and_8_out, and_9_out);
  or or_3 (or_3_out, and_10_out, and_11_out, and_12_out, and_13_out);
  or or_4 (or_4_out, and_14_out, and_15_out, and_16_out, and_17_out);
  not not_37 (not_37_out, a);
  not not_38 (not_38_out, a);
  not not_39 (not_39_out, c);
  not not_40 (not_40_out, b);
  not not_41 (not_41_out, c);
  and and_18 (and_18_out, not_37_out, c);
  and and_19 (and_19_out, not_38_out, b, not_39_out);
  and and_20 (and_20_out, a, not_40_out, not_41_out);
  not not_42 (not_42_out, b);
  not not_43 (not_43_out, a);
  not not_44 (not_44_out, d);
  not not_45 (not_45_out, a);
  not not_46 (not_46_out, d);
  not not_47 (not_47_out, b);
  not not_48 (not_48_out, c);
  not not_49 (not_49_out, d);
  or or_5 (or_5_out, and_18_out, and_19_out, and_20_out);
  and and_21 (and_21_out, not_42_out, not_43_out, not_44_out);
  and and_22 (and_22_out, not_45_out, b, c, not_46_out);
  and and_23 (and_23_out, a, not_47_out, not_48_out, not_49_out);
  not not_50 (not_50_out, a);
  not not_51 (not_51_out, b);
  not not_52 (not_52_out, d);
  not not_53 (not_53_out, a);
  not not_54 (not_54_out, b);
  not not_55 (not_55_out, a);
  not not_56 (not_56_out, c);
  not not_57 (not_57_out, a);
  not not_58 (not_58_out, d);
  not not_59 (not_59_out, b);
  not not_60 (not_60_out, c);
  or or_6 (or_6_out, and_21_out, and_22_out, and_23_out);
  and and_24 (and_24_out, not_50_out, not_51_out, not_52_out);
  and and_25 (and_25_out, not_53_out, not_54_out, c);
  and and_26 (and_26_out, not_55_out, b, not_56_out, d);
  and and_27 (and_27_out, not_57_out, b, c, not_58_out);
  and and_28 (and_28_out, a, not_59_out, not_60_out);
  or or_7 (or_7_out, and_24_out, and_25_out, and_26_out, and_27_out, and_28_out);
  _7_Segment_Display u_7_segment_display_1 (
    .g(or_5_out), .f(or_1_out), .a(or_2_out), .b(or_3_out), .e(or_6_out), .d(or_7_out), .c(or_4_out),
    .dp(in_5));

  // Notes on the sheet:
  //   b
  //   c
  //   a
  //   S3
  //   S7
  //   S2
  //   S4
  //   S5
  //   S6
endmodule
